# Fritzing sketch waterplant (saved by Fritzing 0.9.9b)
breadboards: 1

parts:
  Part1 = Arduino Uno (Rev3)
  Part2 = Soil Moisture Sensor
  M2 = ESP32-C3-DevKitM-1 [part_number=ESP32-C3-DevKitM-1]
  WeMos_D1_Mini_Relay_Shield_V1 = WeMos D1 Mini Relay Shield V2
  U1 = LCD-16X2 [package=lcd-16x2]
  LCM1602_IIC1 = LCM1602 IIC [part_number="LCM1602 IIC" chip_label="LCM1602 IIC" package="DIP (Dual Inline) [THT]"]
  BAT1 = Battery Holders [package=battery-aa]  # not connected
  WATER_PUMP1 = water pump/motor  # not connected

nets:
  N1: Part1.A0, Part2.SIG
  VCC: Part1.A4/SDA, Part1.5V, Part2.VCC, WeMos_D1_Mini_Relay_Shield_V1.3V3, LCM1602_IIC1.VCC, LCM1602_IIC1.SDA
  N2: Part1.A5/SCL, LCM1602_IIC1.SCL
  N3: Part1.D0/RX, M2.TX
  N4: Part1.D1/TX, M2.RX
  N5: Part1.D4, WeMos_D1_Mini_Relay_Shield_V1.D0
  GND: Part1.GND, Part2.GND, WeMos_D1_Mini_Relay_Shield_V1.G, LCM1602_IIC1.GND
  N6: M2.GND-1, M2.GND-4, M2.GND-9, M2.GND-12, M2.GND-15, M2.GND-16, M2.GND-21, M2.GND-23, M2.GND-27, M2.GND-30
  N7: M2.3V3-17, M2.3V3-18
  N8: M2.5V-28, M2.5V-29
  VSS: U1.VSS, LCM1602_IIC1.VSS
  VDD: U1.VDD, LCM1602_IIC1.VDD
  N9: U1.VO, LCM1602_IIC1.V0
  N10: U1.RS, LCM1602_IIC1.RS
  N11: U1.R_W, LCM1602_IIC1.RW
  N12: U1.E, LCM1602_IIC1.E
  N13: U1.DB0, LCM1602_IIC1.D0
  N14: U1.DB1, LCM1602_IIC1.D1
  N15: U1.DB2, LCM1602_IIC1.D2
  N16: U1.DB3, LCM1602_IIC1.D3
  N17: U1.DB4, LCM1602_IIC1.D4
  N18: U1.DB5, LCM1602_IIC1.D5
  N19: U1.DB6, LCM1602_IIC1.D6
  N20: U1.DB7, LCM1602_IIC1.D7
  N21: U1.A, LCM1602_IIC1.A
  N22: U1.K, LCM1602_IIC1.K

notes:
  A
  B
  C
  D
  E
  F
  G
  H

custom parts:
  ESP32-C3-DevKitM-1: Espressif Esp32 DevKit v1 is one of the development board created by DOIT to evaluate the ESP-WROOM-32 module. It is based on the ESP32 microcontroller that boasts Wifi, Bluetooth, Ethernet and Low Power support all in a single chip. (vanepp) Feb 2021: converted to ESP32-C3-DevKitM-1. This chip is 30pins long (2 x15) and 11 pins width.
  LCM1602 IIC: I2C-Module to use a 1602 or 2004 LCD on with the wire.h libory Serial LCD Modul
  water pump/motor: WATER PUMP BY ARDUBLOCKTR
